// Logisim project Registrador AC.circ as structural Verilog: 1 circuit, main circuit main
module main (
  input  [7:0] Barramento_C,
  input  [7:0] Barramento_A
);

  wire ACc_out, ACr_out, ACw_out, clock_1_out, or_1_out;
  wire [7:0] controlled_buffer_1_out, controlled_buffer_2_out, register_1_q;

  assign controlled_buffer_1_out = ACw_out ? Barramento_A : 8'bz;  // Controlled_Buffer controlled_buffer_1
  Button ACc (.out(ACc_out));
  assign controlled_buffer_2_out = ACc_out ? Barramento_C : 8'bz;  // Controlled_Buffer controlled_buffer_2
  assign controlled_buffer_2_out = ACw_out ? controlled_buffer_1_out : 8'bz;  // Controlled_Buffer controlled_buffer_3
  Button ACw (.out(ACw_out));
  or or_1 (or_1_out, ACc_out, ACw_out);
  // Probe on register_1_q
  Register register_1 (.D(controlled_buffer_2_out), .en(or_1_out), .Q(register_1_q), .clk(clock_1_out));  // open: clr
  Clock clock_1 (.out(clock_1_out));
  assign controlled_buffer_1_out = ACr_out ? register_1_q : 8'bz;  // Controlled_Buffer controlled_buffer_4
  Button ACr (.out(ACr_out));
  // Probe on controlled_buffer_1_out

  // Notes on the sheet:
  //   Barramento B
  //   AC
endmodule
