// Logisim project UC Hardwired.circ as structural Verilog: 1 circuit, main circuit main
module main (
  input  [3:0] msb_Barramento_A,
  output ACr,
  output ACw,
  output ACc,
  output PCr,
  output PCw,
  output PC_plus,
  output RIw,
  output REMr,
  output REMw,
  output RDMr,
  output RDMw,
  output RDMrx,
  output RDMwx,
  output nCS,
  output R_nW,
  output [2:0] ULAop
);

  wire and_1_out, decoder_1_out0, decoder_1_out1, decoder_1_out2, decoder_1_out3, decoder_1_out4,
       decoder_1_out5, decoder_1_out6, decoder_1_out7, decoder_1_out8, decoder_1_out9, decoder_1_out10,
       decoder_1_out11, decoder_1_out12, decoder_1_out13, decoder_1_out14, decoder_1_out15, decoder_2_out0,
       decoder_2_out1, decoder_2_out2, decoder_2_out3, decoder_2_out4, decoder_2_out5, decoder_2_out6,
       decoder_2_out7, decoder_2_out8, decoder_2_out9, decoder_2_out10, decoder_2_out11, decoder_2_out12,
       decoder_2_out13, decoder_2_out14, decoder_2_out15, Gerador_de_clock_externo_out, HALTED_q, RIw_out;
  wire [3:0] Contador_de_Sequencia_q, RI_q;

  D_Flip_Flop HALTED (.Q(HALTED_q));  // open: clk, D, Qn, preset, en, reset
  Clock Gerador_de_clock_externo (.out(Gerador_de_clock_externo_out));
  and and_1 (and_1_out, ~HALTED_q, Gerador_de_clock_externo_out);  // AND_Gate
  Button u_RIw (.out(RIw_out));
  Decoder #(.select(4), .enable("false")) decoder_1 (
    .out0(decoder_1_out0), .out1(decoder_1_out1), .out2(decoder_1_out2), .out3(decoder_1_out3),
    .out4(decoder_1_out4), .out5(decoder_1_out5), .out6(decoder_1_out6), .out7(decoder_1_out7),
    .out8(decoder_1_out8), .out9(decoder_1_out9), .out10(decoder_1_out10), .out11(decoder_1_out11),
    .out12(decoder_1_out12), .out13(decoder_1_out13), .out14(decoder_1_out14), .out15(decoder_1_out15),
    .sel(Contador_de_Sequencia_q));
  Counter #(.width(4), .max('hf), .trigger("falling")) Contador_de_Sequencia (
    .count(1'b1), .Q(Contador_de_Sequencia_q), .clk(and_1_out));  // open: load, D, carry, clr
  Register #(.width(4)) RI (.D(msb_Barramento_A), .en(RIw_out), .Q(RI_q), .clk(and_1_out));  // open: clr
  Decoder #(.select(4), .enable("false")) decoder_2 (
    .out0(decoder_2_out0), .out1(decoder_2_out1), .out2(decoder_2_out2), .out3(decoder_2_out3),
    .out4(decoder_2_out4), .out5(decoder_2_out5), .out6(decoder_2_out6), .out7(decoder_2_out7),
    .out8(decoder_2_out8), .out9(decoder_2_out9), .out10(decoder_2_out10), .out11(decoder_2_out11),
    .out12(decoder_2_out12), .out13(decoder_2_out13), .out14(decoder_2_out14), .out15(decoder_2_out15),
    .sel(RI_q));

  // Notes on the sheet:
  //   Decodificador de Sequencia
  //   Decodificador de Instruções
endmodule
